// Logisim project projeto1.circ as structural Verilog: 2 circuits, main circuit main
module main (
  input  x3,
  input  x2,
  input  x1,
  input  x0
);

  wire display_1_f0, display_1_f1, display_1_f2, display_1_f3, display_1_f4, display_1_f5, display_1_f6;

  display display_1 (
    .x3(x3), .x2(x2), .x1(x1), .x0(x0), .f0(display_1_f0), .f1(display_1_f1), .f2(display_1_f2),
    .f3(display_1_f3), .f4(display_1_f4), .f5(display_1_f5), .f6(display_1_f6));
  _7_Segment_Display u_7_segment_display_1 (
    .g(display_1_f3), .f(display_1_f2), .a(display_1_f1), .b(display_1_f0), .e(display_1_f4),
    .d(display_1_f5), .c(display_1_f6));  // open: dp
endmodule

module display (
  input  x3,
  input  x2,
  input  x1,
  input  x0,
  output f0,
  output f1,
  output f2,
  output f3,
  output f4,
  output f5,
  output f6
);

  wire and_1_out, and_2_out, and_3_out, and_4_out, and_5_out, and_6_out, and_7_out, and_8_out, and_9_out,
       and_10_out, and_11_out, and_12_out, and_13_out, and_14_out, and_15_out, and_16_out, not_1_out,
       not_2_out, not_3_out, not_4_out, not_5_out, not_6_out, not_7_out, not_8_out, not_9_out, not_10_out,
       not_11_out, not_12_out, not_13_out, not_14_out, not_15_out, not_16_out, not_17_out, not_18_out,
       not_19_out, not_20_out, not_21_out;

  not not_1 (not_1_out, x2);
  not not_2 (not_2_out, x1);
  and and_1 (and_1_out, not_2_out, not_3_out);
  not not_3 (not_3_out, x0);
  and and_2 (and_2_out, x1, x0);
  not not_4 (not_4_out, x2);
  and and_3 (and_3_out, not_4_out, not_5_out);
  not not_5 (not_5_out, x0);
  and and_4 (and_4_out, x2, x0);
  not not_6 (not_6_out, x1);
  and and_5 (and_5_out, not_6_out, not_7_out);
  not not_7 (not_7_out, x0);
  and and_6 (and_6_out, x2, not_8_out);
  not not_8 (not_8_out, x1);
  and and_7 (and_7_out, x2, not_9_out);
  not not_9 (not_9_out, x0);
  not not_10 (not_10_out, x2);
  and and_8 (and_8_out, not_10_out, x1);
  and and_9 (and_9_out, x1, not_11_out);
  not not_11 (not_11_out, x0);
  and and_10 (and_10_out, x2, not_12_out);
  not not_12 (not_12_out, x1);
  not not_13 (not_13_out, x2);
  and and_11 (and_11_out, not_13_out, not_14_out);
  not not_14 (not_14_out, x0);
  and and_12 (and_12_out, x1, not_15_out);
  not not_15 (not_15_out, x0);
  not not_16 (not_16_out, x2);
  and and_13 (and_13_out, not_16_out, not_17_out);
  not not_17 (not_17_out, x0);
  not not_18 (not_18_out, x2);
  and and_14 (and_14_out, not_18_out, x1);
  and and_15 (and_15_out, x1, not_19_out);
  not not_19 (not_19_out, x0);
  not not_20 (not_20_out, x1);
  and and_16 (and_16_out, x2, not_20_out, x0);
  not not_21 (not_21_out, x1);
  or or_1 (f6, not_21_out, x0, x2);
  or or_2 (f0, not_1_out, and_1_out, and_2_out);
  or or_3 (f1, and_3_out, x1, and_4_out, x3);
  or or_4 (f2, and_5_out, and_6_out, and_7_out, x3);
  or or_5 (f3, and_8_out, and_9_out, and_10_out, x3);
  or or_6 (f4, and_11_out, and_12_out);
  or or_7 (f5, and_13_out, and_14_out, and_15_out, and_16_out, x3);
endmodule
