// Logisim project projeto2.circ as structural Verilog: 3 circuits, main circuit main
module main (
  input  [3:0] a,
  input  So,
  input  [3:0] b,
  output [3:0] c
);

  wire operador_1_overflow_underflow;

  Operador operador_1 (
    .Overflow_underflow(operador_1_overflow_underflow), .S0(So), .c3(c[3]), .c2(c[2]), .c1(c[1]), .c0(c[0]),
    .b3(b[3]), .a3(a[3]), .b2(b[2]), .a2(a[2]), .b1(b[1]), .a1(a[1]), .b0(b[0]), .a0(a[0]));
  LED Overflow_underflow (.in(operador_1_overflow_underflow));
endmodule

module Operador (
  input  S0,
  input  a3,
  input  a2,
  input  a1,
  input  a0,
  input  b3,
  input  b2,
  input  b1,
  input  b0,
  output Overflow_underflow,
  output c3,
  output c2,
  output c1,
  output c0
);

  wire and_1_out, and_2_out, and_3_out, and_4_out, and_5_out, and_6_out, and_7_out, and_8_out, and_9_out,
       and_10_out, not_1_out, not_2_out, not_3_out, not_4_out, not_5_out, not_6_out, not_7_out, not_8_out,
       not_9_out, not_10_out, or_2_out, or_3_out, or_4_out, or_5_out, soma_1bit_1_cout, soma_1bit_2_cout,
       soma_1bit_3_cout, soma_1bit_4_cout;

  or or_1 (Overflow_underflow, and_1_out, and_2_out);
  not not_1 (not_1_out, soma_1bit_2_cout);
  and and_1 (and_1_out, not_1_out, soma_1bit_1_cout);
  and and_2 (and_2_out, soma_1bit_2_cout, not_2_out);
  not not_2 (not_2_out, soma_1bit_1_cout);
  Soma_1bit soma_1bit_1 (.a(or_2_out), .b(a3), .cin(soma_1bit_2_cout), .Si(c3), .cout(soma_1bit_1_cout));
  and and_3 (and_3_out, not_3_out, b3);
  not not_3 (not_3_out, S0);
  Soma_1bit soma_1bit_2 (.a(or_3_out), .b(a2), .cin(soma_1bit_3_cout), .Si(c2), .cout(soma_1bit_2_cout));
  or or_2 (or_2_out, and_3_out, and_4_out);
  and and_4 (and_4_out, S0, not_4_out);
  not not_4 (not_4_out, b3);
  not not_5 (not_5_out, S0);
  Soma_1bit soma_1bit_3 (.a(or_4_out), .b(a1), .cin(soma_1bit_4_cout), .Si(c1), .cout(soma_1bit_3_cout));
  Soma_1bit soma_1bit_4 (.a(or_5_out), .b(a0), .cin(S0), .Si(c0), .cout(soma_1bit_4_cout));
  or or_3 (or_3_out, and_6_out, and_5_out);
  and and_5 (and_5_out, S0, not_6_out);
  and and_6 (and_6_out, not_5_out, b2);
  not not_6 (not_6_out, b2);
  or or_4 (or_4_out, and_7_out, and_8_out);
  and and_7 (and_7_out, not_7_out, b1);
  and and_8 (and_8_out, S0, not_8_out);
  not not_7 (not_7_out, S0);
  not not_8 (not_8_out, b1);
  or or_5 (or_5_out, and_9_out, and_10_out);
  and and_9 (and_9_out, not_10_out, b0);
  and and_10 (and_10_out, S0, not_9_out);
  not not_9 (not_9_out, b0);
  not not_10 (not_10_out, S0);
endmodule

module Soma_1bit (
  input  a,
  input  b,
  input  cin,
  output Si,
  output cout
);

  wire and_1_out, and_2_out, and_3_out, and_4_out, and_5_out, and_6_out, and_7_out, not_1_out, not_2_out,
       not_3_out, not_4_out, not_5_out, not_6_out;

  not not_1 (not_1_out, a);
  not not_2 (not_2_out, b);
  not not_3 (not_3_out, b);
  not not_4 (not_4_out, cin);
  not not_5 (not_5_out, a);
  not not_6 (not_6_out, cin);
  and and_1 (and_1_out, not_1_out, not_2_out, cin);
  and and_2 (and_2_out, a, not_3_out, not_4_out);
  and and_3 (and_3_out, not_5_out, b, not_6_out);
  and and_4 (and_4_out, a, b, cin);
  and and_5 (and_5_out, a, b);
  and and_6 (and_6_out, a, cin);
  and and_7 (and_7_out, b, cin);
  or or_1 (Si, and_1_out, and_2_out, and_3_out, and_4_out);
  or or_2 (cout, and_5_out, and_6_out, and_7_out);
endmodule
